// Logisim project Online 1.circ as structural Verilog: 1 circuit, main circuit 1
// A'D'
module _1 (
  input  A,
  input  B,
  input  C,
  input  D,
  output out_5
);

  wire AND_p2, AND_p3, AND_p4, AND_p6, AND_p7, n7408_1_p3, n7408_1_p11, NOT_p10, OR_p2, OR_p3, OR_p5, OR_p9;

  // _7408 AND: pin names not known; wires that end beside it: 1'b1, AND_p2, AND_p3, AND_p4, AND_p4, AND_p6, AND_p7, 1'b0, 1'b1
  // _7432 OR: pin names not known; wires that end beside it: AND_p7, OR_p2, OR_p3, OR_p3, OR_p5, out_5, 1'b0, 1'b1, OR_p9, C, AND_p6
  // _7404 NOT: pin names not known; wires that end beside it: AND_p2, A, AND_p2, B, OR_p9, 1'b0, OR_p9, 1'b1, C, NOT_p10, D, AND_p3, NOT_p10, AND_p3
  // _7408 7408_1: pin names not known; wires that end beside it: A, B, n7408_1_p3, n7408_1_p3, D, OR_p2, 1'b0, 1'b1, A, C, n7408_1_p11, n7408_1_p11, D, OR_p5, 1'b0
endmodule
